# Fritzing sketch laboite (saved by Fritzing 0.9.2b)
breadboards: 1

parts:
  8x8_LED_Modul_mit_MAX1 = 8x8 LED Modul mit MAX7219 [package=THT]
  8x8_LED_Modul_mit_MAX2 = 8x8 LED Modul mit MAX7219 [package=THT]  # not connected
  8x8_LED_Modul_mit_MAX3 = 8x8 LED Modul mit MAX7219 [package=THT]  # not connected
  8x8_LED_Modul_mit_MAX4 = 8x8 LED Modul mit MAX7219 [package=THT]
  8x8_LED_Modul_mit_MAX5 = 8x8 LED Modul mit MAX7219 [package=THT]  # not connected
  8x8_LED_Modul_mit_MAX6 = 8x8 LED Modul mit MAX7219 [package=THT]  # not connected
  8x8_LED_Modul_mit_MAX7 = 8x8 LED Modul mit MAX7219 [package=THT]  # not connected
  8x8_LED_Modul_mit_MAX8 = 8x8 LED Modul mit MAX7219 [package=THT]
  U1 = NodeMCU V3.0

nets:
  N1: 8x8_LED_Modul_mit_MAX1.VCC_Eingang, U1.Vin
  N2: 8x8_LED_Modul_mit_MAX1.GND_Eingang, U1.GND#6, U1.GND#13, U1.GND#16, U1.GND#33
  N3: 8x8_LED_Modul_mit_MAX1.DIN_Eingang, U1.D7
  N4: 8x8_LED_Modul_mit_MAX1.CS_Eingang, U1.D8
  N5: 8x8_LED_Modul_mit_MAX1.CLK_Eingang, U1.D5
  N6: 8x8_LED_Modul_mit_MAX4.VCC_Ausgang, 8x8_LED_Modul_mit_MAX8.VCC_Eingang
  N7: 8x8_LED_Modul_mit_MAX4.GND_Ausgang, 8x8_LED_Modul_mit_MAX8.GND_Eingang
  N8: 8x8_LED_Modul_mit_MAX4.DOUT_Ausgang, 8x8_LED_Modul_mit_MAX8.DIN_Eingang
  N9: 8x8_LED_Modul_mit_MAX4.CS_Ausgang, 8x8_LED_Modul_mit_MAX8.CS_Eingang
  N10: 8x8_LED_Modul_mit_MAX4.CLK_Ausgang, 8x8_LED_Modul_mit_MAX8.CLK_Eingang

custom parts:
  NodeMCU V3.0: ESP8266 based NodeMCU
